# Fritzing sketch exercise_work_2 (saved by Fritzing 0.9.3b)
breadboards: 1

parts:
  Part1 = Arduino Uno (Rev3)
  Part2 = Arduino Mega 2560 (Rev3)
  LCD1 = LCD screen
  R1 = Trimmer Potentiometer [maximum_resistance=10kΩ package=THT]
  R4 = Motion sensor [package=THT]
  IC1 = SHIFT REGISTER [package=so16]

nets:
  N1: Part1.A4/SDA, Part2.D20/SDA, Part2.SDA
  N2: Part1.A5/SCL, Part2.D21/SCL, Part2.SCL
  N3: Part1.D8, LCD1.DB7
  N4: Part1.D2, LCD1.RS
  N5: Part1.D3_PWM, LCD1.E
  N6: Part1.D5_PWM, LCD1.DB4
  N7: Part1.D6_PWM, LCD1.DB5
  N8: Part1.D7, LCD1.DB6
  GND: Part1.GND, Part2.GND, LCD1.VSS, LCD1.R/W, LCD1.LED-, R1.leg1, R4.wiper
  N9: Part2.D10_PWM, R4.leg2
  N10: Part2.D9_PWM, IC1.GND
  N11: Part2.D8_PWM, IC1.QH
  N12: Part2.D2_PWM, IC1.QB
  N13: Part2.D3_PWM, IC1.QC
  N14: Part2.D4_PWM, IC1.QD
  N15: Part2.D5_PWM, IC1.QE
  N16: Part2.D6_PWM, IC1.QF
  N17: Part2.D7_PWM, IC1.QG
  N18: LCD1.VDD, LCD1.LED+, R1.leg2, R4.leg1
  N19: LCD1.V0, R1.wiper

custom parts:
  Motion sensor: A standard 6mm trimmer potentiometer.
